# Fritzing sketch secureembedded 2 (saved by Fritzing 0.9.3b)
breadboards: 1

parts:
  S1 = Pushbutton [package="[THT]"]
  R1 = Resistor [tolerance=±5% resistance=220 package=THT]
  R2 = Resistor [tolerance=±5% resistance=220 package=THT]
  Part1 = Intel Edison Arduinobreakout
  LED1 = smd LED [color="Red (633nm)" package="1206 [SMD]"]
  LED2 = smd LED [color="Red (633nm)" package="1206 [SMD]"]
  R3 = Resistor [tolerance=±5% resistance=220 package=THT]

nets:
  N1: S1.Pin_1, S1.Pin_2, Part1.5V
  N2: S1.Pin_3, S1.Pin_4, Part1.D3_PWM, R3.Pin_0, R3.Pin_1
  N3: R1.Pin_0, Part1.D2
  N4: R1.Pin_1, LED1.cathode
  N5: R2.Pin_0, Part1.D4
  N6: R2.Pin_1, LED2.cathode
  N7: Part1.GND, LED1.anode, LED2.anode
