# Fritzing sketch part1 (saved by Fritzing 0.9.3b)
breadboards: 1

parts:
  Part1 = Intel Edison Arduinobreakout
  S1 = Pushbutton [package="[SMD]"]
  S2 = Pushbutton [package="[SMD]"]
  R1 = Resistor [tolerance=±5% resistance=220 package=THT]
  R2 = Resistor [tolerance=±5% resistance=220 package=THT]

nets:
  N1: Part1.D2, S2.Pin_1, S2.Pin_2, R1.Pin_0, R1.Pin_1
  N2: Part1.D4, S1.Pin_1, S1.Pin_2, R2.Pin_0, R2.Pin_1
  N3: Part1.5V, S1.Pin_3, S1.Pin_4, S2.Pin_3, S2.Pin_4
